# Fritzing sketch LedRGB_pot (saved by Fritzing 0.9.9b)
breadboards: 1

parts:
  Componente1 = Arduino Uno (Rev3)
  Mod1 = KY-016 RGB Full Color LED Module [package="Breakout board"]
  R1 = Rotary Potentiometer (Small) [maximum_resistance=100kΩ package=THT]

nets:
  N1: Componente1.A0, R1.wiper
  N2: Componente1.D9_PWM, Mod1.B
  N3: Componente1.D10_PWM/SS, Mod1.G
  N4: Componente1.D11_PWM/MOSI, Mod1.R
  N5: Componente1.GND, Mod1.-, R1.leg2
  N6: Componente1.5V, R1.leg1

custom parts:
  KY-016 RGB Full Color LED Module: KY-016 Arduino full color 5mm RGB LED, different colors can be obtained by mixing the three primary colors.
