# Fritzing sketch Led_switch (saved by Fritzing 0.9.9b)
breadboards: 1

parts:
  LED1 = LED - 5mm [color="Red (633nm)" package="5 mm [THT]"]
  part = Arduino Uno (Rev3)
  R1 = Resistor [tolerance=±5% resistance=220 package=THT]
  part_2 = Pushbutton [package="[THT]"]

nets:
  N1: LED1.cathode, part.GND
  N2: LED1.anode, R1.Pin_0
  N3: part.5V, part_2.Pin_1, part_2.Pin_2
  N4: R1.Pin_1, part_2.Pin_3, part_2.Pin_4
