# Fritzing sketch Led_switchPot (saved by Fritzing 0.9.9b)
breadboards: 1

parts:
  LED1 = LED - 5mm [color="Red (633nm)" package="5 mm [THT]"]
  Arduino = Arduino Uno (Rev3)
  R1 = Resistor [tolerance=±5% resistance=220 package=THT]
  S1 = Pushbutton [package="[THT]"]
  R2 = Rotary Potentiometer (Small) [maximum_resistance=10kΩ package=THT]

nets:
  N1: LED1.cathode, Arduino.GND
  N2: LED1.anode, R1.Pin_0
  N3: Arduino.5V, R2.leg2
  N4: R1.Pin_1, S1.Pin_3
  N5: S1.Pin_1, S1.Pin_2, R2.wiper
