# Fritzing sketch led_RGB_2 (saved by Fritzing 0.9.9b)
breadboards: 1

parts:
  LED1 = RGB LED (com. cathode, rgb) [package="5 mm [THT]"]
  R2 = Resistor [tolerance=±5% resistance=220 package=THT]
  R3 = Resistor [tolerance=±5% resistance=220 package=THT]
  R4 = Resistor [tolerance=±5% resistance=220 package=THT]
  Componente2 = Arduino Uno (Rev3)

nets:
  N1: LED1.red_anode, R2.Pin_1
  N2: LED1.common_cathode, Componente2.GND
  N3: LED1.green_anode, R3.Pin_1
  N4: LED1.blue_anode, R4.Pin_1
  N5: R2.Pin_0, Componente2.D11_PWM/MOSI
  N6: R3.Pin_0, Componente2.D10_PWM/SS
  N7: R4.Pin_0, Componente2.D9_PWM

custom parts:
  RGB LED (com. cathode, rgb): A 5mm tri-color LED with red, green and blue inside.
